# Fritzing sketch Schema (saved by Fritzing 0.8.7b)
breadboards: 1

parts:
  S2 = H-Bridge with L298N
  VCC2 = Battery block 9V
  M3 = DC Motor
  M4 = DC Motor  # not connected
  M5 = DC Motor
  M6 = DC Motor  # not connected
  Part1 = Arduino Uno (Rev3)
  Part2 = Bluetooth HC-05 Macho  # not connected
  LED1 = LED - 5mm [color="Orange (605nm)" package="5 mm [THT]"]
  LED2 = LED - 5mm [color="Red (633nm)" package="5 mm [THT]"]
  LED3 = LED - 5mm [color="White (4500K)" package="5 mm [THT]"]
  LED4 = LED - 5mm [color="Orange (605nm)" package="5 mm [THT]"]
  LED5 = LED - 5mm [color="White (4500K)" package="5 mm [THT]"]  # not connected
  LED6 = LED - 5mm [color="Red (633nm)" package="5 mm [THT]"]  # not connected
  LED7 = LED - 5mm [color="White (4500K)" package="5 mm [THT]"]  # not connected
  LED8 = LED - 5mm [color="Green (555nm)" package="5 mm [THT]"]
  LED9 = LED - 5mm [color="White (4500K)" package="5 mm [THT]"]
  LED10 = LED - 5mm [color="Orange (605nm)" package="5 mm [THT]"]
  LED11 = LED - 5mm [color="Orange (605nm)" package="5 mm [THT]"]
  LED12 = LED - 5mm [color="Green (555nm)" package="5 mm [THT]"]
  LED13 = LED - 5mm [color="Green (555nm)" package="5 mm [THT]"]
  LED14 = LED - 5mm [color="Green (555nm)" package="5 mm [THT]"]
  R1 = Resistor [tolerance=±5% resistance=220 package=THT]
  R2 = Resistor [tolerance=±5% resistance=220 package=THT]
  Solar_Cell = Solar Cell
  X2 = USB Connectors [package=usb-a-s]
  M7 = bb-usb-cable [package=THT]  # not connected
  TP4056 = TP4056 [chip_label=TP4056 package="DIP (Dual Inline) [THT]"]
  U1 = LIPO-1000mAh [package=lipo-1000]
  Convert_3_7V_to_5V = DC-DC CONVERTER [part_number=80633 package=dc-dc_converter]

nets:
  N1: S2.12V, VCC2.+
  5V: S2.5V, Part1.5V
  N2: S2.OUT4-Motor2, M3.pin_1, M5.pin_1
  N3: Part1.D8, LED4.anode, LED10.anode
  N4: Part1.D9_PWM, LED1.anode, LED11.anode
  N5: Part1.GND, LED8.anode, LED13.anode, LED14.cathode
  N6: Part1.D3_PWM, R1.Pin_1
  N7: Part1.D4, LED3.anode
  N8: Part1.D5_PWM, LED2.anode
  N9: Part1.D6_PWM, LED9.anode
  N10: Part1.D7, LED12.anode, LED14.anode
  N11: R1.Pin_0, R2.Pin_0, R2.Pin_1
  N12: Solar_Cell.+, TP4056.pin1
  N13: Solar_Cell.-, TP4056.pin2
  N14: X2.GND, Convert_3_7V_to_5V.OUT-
  N15: X2.VBUS, Convert_3_7V_to_5V.OUT+
  N16: TP4056.pin3, Convert_3_7V_to_5V.IN+
  N17: TP4056.pin4, U1.+
  N18: TP4056.pin6, Convert_3_7V_to_5V.IN-

custom parts:
  H-Bridge with L298N: h-bridge
  bb-usb-cable: Breadboard only, no connectors USB cable for the Raspberry PIs.
  TP4056: A DIP stand-in part for whatever IC you want. With 6 pins on a 300mil dual inline package (DIP) footprint.
  DC-DC CONVERTER: WYHP 5A constant current/voltage manufactured by Shenzhen Weiyapuhua Technology Co., Ltd
